// Logisim project NAND2Tetris.circ as structural Verilog: 5 circuits, main circuit ALU
module main (
  input  [15:0] in_1,
  input  [15:0] in_2,
  output out_3
);

  wire button_1_out;
  wire [15:0] undriven, undriven_2;

  Button button_1 (.out(button_1_out));
  // Probe on in_1[15:8]
  // Probe on in_1[7:0]
  // Probe on in_2[15:8]
  // Probe on in_2[7:0]
  sw sw_1 (.in_3(button_1_out));  // open: in_1, in_2
  // Probe on undriven[15:8]
  // Probe on undriven_2[15:8]
  // Probe on undriven[7:0]
  // Probe on undriven_2[7:0]

  // Notes on the sheet:
  //   in_2: pull=down
  //   in_1: pull=down
endmodule

module ALU (
  input  [15:0] x,
  input  [15:0] y,
  input  zx,
  input  nx,
  input  zy,
  input  ny,
  input  f,
  input  no,
  output [15:0] out,
  output zr,
  output ng
);

  wire NO_t, NX_t, NY_t, ZX_t, ZY_t;
  wire [15:0] adder_1_out, and_1_out, and_2_out, and_3_out, multiplexer_1_out, multiplexer_2_out,
       multiplexer_3_out, multiplexer_4_out, multiplexer_5_out, not_6_out, not_7_out, not_8_out, not_9_out,
       not_10_out;

  not not_1 (ZX_t, zx);
  not not_2 (NX_t, nx);
  not not_3 (ZY_t, zy);
  not not_4 (NY_t, ny);
  not not_5 (NO_t, no);
  assign not_6_out = ~x;  // NOT_Gate not_6, 16 bits wide
  // Probe on not_6_out
  assign and_1_out = not_6_out & x;  // AND_Gate and_1, 16 bits wide
  // Probe on not_7_out
  assign not_7_out = ~y;  // NOT_Gate not_7, 16 bits wide
  assign and_2_out = not_7_out & y;  // AND_Gate and_2, 16 bits wide
  // Probe on and_1_out
  // Probe on multiplexer_1_out
  Multiplexer #(.width(16), .enable("false")) multiplexer_1 (
    .in0(and_1_out), .in1(x), .out(multiplexer_1_out), .sel(ZX_t));
  // Probe on and_2_out
  assign not_8_out = ~multiplexer_1_out;  // NOT_Gate not_8, 16 bits wide
  // Probe on multiplexer_2_out
  Multiplexer #(.width(16), .enable("false")) multiplexer_2 (
    .in0(and_2_out), .in1(y), .out(multiplexer_2_out), .sel(ZY_t));
  assign not_9_out = ~multiplexer_2_out;  // NOT_Gate not_9, 16 bits wide
  Multiplexer #(.width(16), .enable("false")) multiplexer_3 (
    .in0(not_8_out), .in1(multiplexer_1_out), .out(multiplexer_3_out), .sel(NX_t));
  Multiplexer #(.width(16), .enable("false")) multiplexer_4 (
    .in0(not_9_out), .in1(multiplexer_2_out), .out(multiplexer_4_out), .sel(NY_t));
  assign and_3_out = multiplexer_4_out & multiplexer_3_out;  // AND_Gate and_3, 16 bits wide
  Adder #(.width(16)) adder_1 (.a(multiplexer_4_out), .b(multiplexer_3_out), .out(adder_1_out));  // open: cin, cout
  Multiplexer #(.width(16), .enable("false")) multiplexer_5 (
    .in0(and_3_out), .in1(adder_1_out), .out(multiplexer_5_out), .sel(f));
  Comparator #(.width(16), .mode("unsigned")) comparator_1 (.a(out), .b({16{1'b0}}), .eq(zr));  // open: gt, lt
  BitSelector #(.width(16)) bitselector_1 (.in(out), .out(ng), .sel(4'b1111));
  assign not_10_out = ~multiplexer_5_out;  // NOT_Gate not_10, 16 bits wide
  Multiplexer #(.width(16), .enable("false")) multiplexer_6 (
    .in0(not_10_out), .in1(multiplexer_5_out), .out(out), .sel(NO_t));

  // Notes on the sheet:
  //   f: pull=down
  //   y: pull=down
  //   x: pull=down
  //   ny: pull=down
  //   zx: pull=down
  //   zy: pull=down
  //   nx: pull=down
  //   no: pull=down
endmodule

// ALU
module CPU (
  input  [15:0] inM,
  input  [15:0] instruction,
  input  reset,
  output [15:0] outM,
  output [15:0] addressM,
  output [15:0] PC,
  output writeM
);

  wire alu_1_ng, alu_1_zr, and_1_out, and_2_out, and_3_out, and_4_out, F, JMP_out, not_1_out, not_2_out, NX,
       NY, or_1_out, or_3_out, or_4_out, T, undriven, WPC, ZX, ZY;
  wire [15:0] D_2_q, multiplexer_1_out, multiplexer_2_out;

  Clock clock_1 (.out(T));
  not not_1 (not_1_out, instruction[15]);
  Multiplexer #(.width(16), .disabled(0), .enable("false")) multiplexer_1 (
    .in0(outM), .in1(instruction), .out(multiplexer_1_out), .sel(not_1_out));
  or or_1 (or_1_out, ~instruction[15], instruction[5]);  // OR_Gate
  not not_2 (not_2_out, WPC);
  Register #(.width(16)) A (.D(multiplexer_1_out), .en(or_1_out), .Q(addressM), .clk(T));  // open: clr
  or or_2 (F, or_3_out, instruction[7]);
  Multiplexer #(.width(16), .disabled(0), .enable("false")) multiplexer_2 (
    .in0(addressM), .in1(inM), .out(multiplexer_2_out), .sel(instruction[12]));
  Counter #(.width(16), .max('hffff), .ongoal("stay")) u_PC (
    .load(WPC), .D(addressM), .count(not_2_out), .Q(PC), .clk(T), .clr(reset));  // open: carry
  and D (ZY, instruction[8], instruction[9]);
  and A_M (ZX, instruction[10], instruction[11]);
  or or_3 (or_3_out, ZX, ZY);
  // Probe on outM
  Register #(.width(16)) D_2 (.D(outM), .en(instruction[4]), .Q(D_2_q), .clk(T));  // open: clr
  ALU alu_1 (
    .x(D_2_q), .y(multiplexer_2_out), .zx(ZX), .nx(NX), .zy(ZY), .ny(NY), .f(F), .no(undriven), .out(outM),
    .zr(alu_1_zr), .ng(alu_1_ng));
  and and_1 (and_1_out, alu_1_zr, instruction[1]);
  and and_2 (and_2_out, ~alu_1_ng, ~alu_1_zr, instruction[0]);  // AND_Gate
  and and_3 (and_3_out, alu_1_ng, ~alu_1_zr, instruction[2]);  // AND_Gate
  and JMP (JMP_out, instruction[0], instruction[1], instruction[2]);
  or or_4 (or_4_out, and_2_out, and_3_out);
  or or_5 (WPC, and_1_out, and_2_out, and_4_out, JMP_out);
  and and_4 (and_4_out, ~instruction[1], or_4_out);  // AND_Gate

  assign writeM = instruction[3];

  // Other names for the same wires on the sheet: GTZ = instruction[0]; EQZ = instruction[1]; LTZ = instruction[2];
  //   WM = instruction[3]; WD = instruction[4]; WA = instruction[5]; a = instruction[12]; bit1 = instruction[15];
  //   M[15:0] = inM; R = reset

  // Notes on the sheet:
  //   inM: pull=down
  //   reset: pull=down
  //   instruction: pull=down
  //   writeM: pull=down
endmodule

module FullAdder (
  input  x,
  input  y,
  input  z,
  output a1,
  output a2
);

  wire and_1_out, and_2_out, and_3_out, and_4_out, and_5_out, and_6_out, and_7_out, and_8_out, and_9_out,
       not_1_out, not_2_out, not_3_out, not_4_out, not_5_out, not_6_out, or_1_out, or_2_out, or_3_out,
       or_4_out, or_5_out;

  not not_1 (not_1_out, x);
  not not_2 (not_2_out, y);
  not not_3 (not_3_out, x);
  not not_4 (not_4_out, y);
  or or_1 (or_1_out, x, y);
  or or_2 (or_2_out, x, z);
  and and_1 (and_1_out, not_1_out, not_2_out);
  and and_2 (and_2_out, not_3_out, y);
  not not_5 (not_5_out, z);
  and and_3 (and_3_out, x, not_4_out);
  not not_6 (not_6_out, z);
  and and_4 (and_4_out, x, y);
  and and_5 (and_5_out, or_1_out, or_2_out);
  or or_3 (or_3_out, y, z);
  and and_6 (and_6_out, and_1_out, z);
  and and_7 (and_7_out, and_2_out, not_5_out);
  and and_8 (and_8_out, and_3_out, not_6_out);
  and and_9 (and_9_out, and_4_out, z);
  and and_10 (a2, and_5_out, or_3_out);
  or or_4 (or_4_out, and_6_out, and_7_out);
  or or_5 (or_5_out, and_8_out, and_9_out);
  or or_6 (a1, or_4_out, or_5_out);
endmodule

module sw (
  input  in_1,
  input  in_2,
  input  in_3
);

  Hex_Digit_Display hex_digit_display_1 ();  // open: value, dp
endmodule
