// Logisim project NAND2Tetris_CPU.circ as structural Verilog: 1 circuit, main circuit CPU
module CPU (
  input  [15:0] inM,
  input  [15:0] instruction,
  input  reset,
  output [15:0] outM,
  output writeM,
  output [14:0] addressM,
  output [14:0] pc
);
endmodule
